# Fritzing sketch Hall_Circuit US1881 (saved by Fritzing 0.9.3b)

parts:
  ESC = ESC
  BLDC_Motor = DJI 920 KV Motor
  Power_plug2 = Power plug  # not connected
  Arduino_Nano = Arduino Nano (Rev3.0)
  0_01uF_(103) = Capacitor [package=cap-pth-5mm]
  US1881 = TRANSISTOR_PNP [package=to-92]
  R2 = Resistor [tolerance=±5% resistance=10k package="0603 [SMD]"]

nets:
  N1: ESC.U, BLDC_Motor.u
  N2: ESC.V, BLDC_Motor.v
  N3: ESC.W, BLDC_Motor.w
  N4: ESC.DATA, Arduino_Nano.D9
  GND: ESC.GND, Arduino_Nano.GND, 0_01uF_(103).2, US1881.B
  N5: Arduino_Nano.D2, 0_01uF_(103).1, US1881.C, R2.Pin_1
  N6: Arduino_Nano.5V, US1881.E, R2.Pin_0

custom parts:
  DJI 920 KV Motor: DJI Brushless Outrunner 2212/920K Motor F330-550
