# Fritzing sketch Hall_Circuit (saved by Fritzing 0.9.3b)

parts:
  ESC = ESC
  BLDC_Motor = DJI 920 KV Motor
  Power_plug2 = Power plug  # not connected
  kY-024 = KY-024 Linear Hall Magnetic Sensor Module [package="Breakout board"]
  Arduino_Nano = Arduino Nano (Rev3.0)
  0_01uF_(103) = Capacitor [package=cap-pth-5mm]

nets:
  N1: ESC.U, BLDC_Motor.u
  N2: ESC.V, BLDC_Motor.v
  N3: ESC.W, BLDC_Motor.w
  N4: ESC.DATA, Arduino_Nano.D9
  GND: ESC.GND, kY-024.G, Arduino_Nano.GND, 0_01uF_(103).2
  N5: kY-024.+, Arduino_Nano.5V
  N6: kY-024.D0, Arduino_Nano.D2, 0_01uF_(103).1

custom parts:
  DJI 920 KV Motor: DJI Brushless Outrunner 2212/920K Motor F330-550
  KY-024 Linear Hall Magnetic Sensor Module: KEYES KY-024 Arduino Linear Hall Magnetic Sensor Module reacts iin the presence of a magnetic field.
