# Fritzing sketch IR_Circuit (saved by Fritzing 0.9.3b)

parts:
  ESC = ESC
  BLDC_Motor = DJI 920 KV Motor
  Power_plug2 = Power plug  # not connected
  Arduino_nano = Arduino Nano (Rev3.0)
  0_01uF_(103) = Capacitor [package=cap-pth-5mm]
  FC-51 = fc-51 [package=THT]

nets:
  N1: ESC.U, BLDC_Motor.u
  N2: ESC.V, BLDC_Motor.v
  N3: ESC.W, BLDC_Motor.w
  N4: ESC.DATA, Arduino_nano.D9
  GND: ESC.GND, Arduino_nano.GND, 0_01uF_(103).2, FC-51.pin2
  N5: Arduino_nano.D2, 0_01uF_(103).1
  N6: Arduino_nano.5V, FC-51.pin3

custom parts:
  DJI 920 KV Motor: DJI Brushless Outrunner 2212/920K Motor F330-550
