# Fritzing sketch circuit (saved by Fritzing 0.9.3b)

parts:
  M1 = ESC
  920KV_Motor1 = DJI 920 KV Motor
  Power_plug2 = Power plug  # not connected
  kY-024 = KY-024
  Part3 = Arduino Nano (Rev3.0)
  0_1uF_(104) = Capacitor [package=cap-pth-5mm]

nets:
  N1: M1.U, 920KV_Motor1.u
  N2: M1.V, 920KV_Motor1.v
  N3: M1.W, 920KV_Motor1.w
  N4: M1.DATA, Part3.D9
  GND: M1.GND, kY-024.connector1, Part3.GND, 0_1uF_(104).2
  N5: kY-024.connector2, Part3.5V
  N6: Part3.D2, 0_1uF_(104).1

custom parts:
  DJI 920 KV Motor: DJI Brushless Outrunner 2212/920K Motor F330-550
